# Fritzing sketch wemos_esp12f (saved by Fritzing 0.9.6b)
breadboards: 1

parts:
  WeMos_D1_Mini1 = WeMos D1 Mini  # not connected
  IC1 = L293D [package=THT]
  VCC1 = 4 x AAA Battery Mount
  M1 = Getriebemotor
  M2 = Getriebemotor

nets:
  N1: IC1.Out_1_(_Controlled_by_Enable_1_), M1.pin_2
  N2: IC1.0V, VCC1.-
  N3: IC1.Out_2_(_Controlled_by_Enable_1_), M1.pin_1
  N4: IC1.Out_3_(_Controlled_by_Enable_2_), M2.pin_2
  N5: IC1.Out_4_(_Controlled_by_Enable_2_), M2.pin_1
  N6: IC1.+V, VCC1.+
